# Fritzing sketch Circuit (saved by Fritzing 0.9.5d)
breadboards: 1

parts:
  Raspberry_Pi_1 = Raspberry Pi 3 [part_number=RPI-3-V1.2]
  S1 = Square Pushbutton

nets:
  N1: Raspberry_Pi_1.GIPO23, S1.leg1
  N2: Raspberry_Pi_1.GND, S1.leg0

notes:
  Console Button
  GPIO23
